// Logisim project full-adder.circ as structural Verilog: 1 circuit, main circuit full-adder
module full_adder (
  input  Cin,
  input  A,
  input  B,
  output S,
  output Cout
);

  wire half_adder_1_cout, half_adder_1_s, half_adder_2_cout;

  half_adder half_adder_1 (.A(A), .B(B), .S(half_adder_1_s), .Cout(half_adder_1_cout));
  or or_1 (Cout, half_adder_1_cout, half_adder_2_cout);
  half_adder half_adder_2 (.A(half_adder_1_s), .B(Cin), .S(S), .Cout(half_adder_2_cout));
endmodule
