// Logisim project add-8bit.circ as structural Verilog: 1 circuit, main circuit add-8bit
module add_8bit (
  input  Cin,
  input  [7:0] A,
  input  [7:0] B,
  output [7:0] S,
  output Cout
);

  wire full_adder_1_cout, full_adder_2_cout, full_adder_3_cout, full_adder_4_cout, full_adder_5_cout,
       full_adder_6_cout, full_adder_7_cout;

  full_adder full_adder_1 (.A(A[0]), .B(B[0]), .S(S[0]), .Cin(Cin), .Cout(full_adder_1_cout));
  full_adder full_adder_2 (.A(A[1]), .B(B[1]), .S(S[1]), .Cin(full_adder_1_cout), .Cout(full_adder_2_cout));
  full_adder full_adder_3 (.A(A[2]), .B(B[2]), .S(S[2]), .Cin(full_adder_2_cout), .Cout(full_adder_3_cout));
  full_adder full_adder_4 (.A(A[3]), .B(B[3]), .S(S[3]), .Cin(full_adder_3_cout), .Cout(full_adder_4_cout));
  full_adder full_adder_5 (.A(A[4]), .B(B[4]), .S(S[4]), .Cin(full_adder_4_cout), .Cout(full_adder_5_cout));
  full_adder full_adder_6 (.A(A[5]), .B(B[5]), .S(S[5]), .Cin(full_adder_5_cout), .Cout(full_adder_6_cout));
  full_adder full_adder_7 (.A(A[6]), .B(B[6]), .S(S[6]), .Cin(full_adder_6_cout), .Cout(full_adder_7_cout));
  full_adder full_adder_8 (.A(A[7]), .B(B[7]), .S(S[7]), .Cin(full_adder_7_cout), .Cout(Cout));
endmodule
